# Fritzing sketch Pressure Sensor (saved by Fritzing 0.9.4)
breadboards: 1

parts:
  Part1 = Arduino Uno (Rev3)
  J1 = Basic Force Sensing Resistor (FSR) [package=THT]
  R1 = Resistor [tolerance=±5% resistance=220 package=THT]
  LED1 = LED - 5mm [color="Red (633nm)" package="5 mm [THT]"]
  R2 = Resistor [tolerance=±5% resistance=220 package=THT]

nets:
  N1: Part1.A0, J1.pin_0, R1.Pin_1
  N2: Part1.D11_PWM/MOSI, LED1.anode
  N3: Part1.5V, J1.pin_1
  N4: Part1.GND, R1.Pin_0, R2.Pin_1
  N5: LED1.cathode, R2.Pin_0

// code stored in the sketch: Pressure Sensor.ino
/* FSR simple testing sketch.  <br>Connect one end of FSR to power, the other end to Analog 0.
Then connect one end of a 10K resistor from Analog 0 to ground 
*/
int fsrPin = 0;     // the FSR and 10K pulldown are connected to a0
int fsrReading;     // the analog reading from the FSR resistor divider
 
void setup(void) {
  Serial.begin(9600);   
}
 
void loop(void) {
  fsrReading = analogRead(fsrPin);  
 
  Serial.print("Analog reading = ");
  Serial.print(fsrReading);     // the raw analog reading
 
 
  if (fsrReading == 0) {
    Serial.println(" - No pressure");
  } else if (fsrReading < 10) {
    Serial.println(" - Light touch");
  } else if (fsrReading < 50) {
    Serial.println(" - Light squeeze");
  } else if (fsrReading < 150) {
    Serial.println(" - Medium squeeze");
  } else {
    Serial.println(" - Big squeeze");
  }
  delay(1000);
}
